# Fritzing sketch Verbindung (saved by Fritzing 0.9.3b)
perfboards: 1

parts:
  JACK1 = 2.1mm Barrel Jack with Terminal Block
  VALVE1 = Plastic Solenoid Valve
  M1 = RioRand LM2596
  Mod1 = KY-019 5V Relay Module [package="Breakout board"]
  U1 = ATTINY45 [package=dip]
  RXB1 = RXB14

nets:
  N1: JACK1.POS, M1.Pin_2, Mod1.Common
  N2: JACK1.NEG, VALVE1.no_name_yet#1, M1.Pin_1
  N3: VALVE1.no_name_yet#2, Mod1.NO
  N4: M1.Pin_3, Mod1.+, U1.VCC, RXB1.pin_1
  N5: M1.Pin_4, Mod1.-, U1.GND, RXB1.pin_3
  N6: Mod1.S, U1.PB2(SCK_ADC1)
  N7: U1.PB1(MISO), RXB1.pin_2

custom parts:
  KY-019 5V Relay Module: KY-019 5V Relay module, used to control AC circuits. (Special thanks to vanepp for fixing the PCB holes and other errors)
  RXB14: RXB14 433mhz Empfangsmodul
